# Fritzing sketch homemade laser tag (saved by Fritzing 0.9.3b)

parts:
  Arduino_Nano_1 = Arduino Nano (Rev3.0)
  Infrared_LED_1 = LEDs [package=led10mm]  # not connected
  Part1 = Infra red receiver
  Part2 = Infra red receiver  # not connected
  Part3 = Infra red receiver  # not connected
  Part4 = Infra red receiver  # not connected
  Part5 = Infra red receiver  # not connected
  D2F1 = D2F-FL Omron Snap Action Limit Switch with Level  # not connected
  S1 = Momentary Switch [package=ksa_sealed_tac_switch]  # not connected
  U6 = RF-LINK_TX [package=rf-link_tx]
  U7 = RF-LINK_RX [package=rf-link_rx]
  VCC1 = Battery block 9V
  LED1 = RGB LED - (4 legs) [package="5 mm [THT]"]  # not connected
  S2 = SWITCH-SPST-2 [package=switch-spst-vertical]
  Squix1 = OLED 0.96" 128x64 I2C SSD1306

nets:
  GND: Arduino_Nano_1.GND, Part1.GND, U6.GND, Squix1.GND
  N1: Arduino_Nano_1.D10, U6.DATA
  N2: Arduino_Nano_1.D11/MOSI, Part1.Data
  N3: Arduino_Nano_1.D12/MISO, U7.Data
  N4: Arduino_Nano_1.VIN, S2.O
  VCC: Arduino_Nano_1.5V, Part1.VCC, U6.+5V, U7.VCC
  N5: Arduino_Nano_1.A5, Squix1.SCL
  N6: Arduino_Nano_1.A4, Squix1.SCA
  N7: U7.GND, VCC1.-
  N8: VCC1.+, S2.P

notes:
  all components without connections have yet to be assinged pins
  the 3rd pin is intentionally not connected

custom parts:
  D2F-FL Omron Snap Action Limit Switch with Level: Snap action switch with stainless steel lever.
  RF-LINK_TX: Common RF transmitter of the 315.00Mhz varity
  RF-LINK_RX: RF Link receivers- WRL-8947, 8948, 8949, 8950
